# Fritzing sketch AutoPlanter (saved by Fritzing 1.0.7)
breadboards: 1

parts:
  Part1 = Node32s
  IC1 = Picobuck [chip_label=IC package="DIP (Dual Inline) [THT]"]
  Q1 = PNP-Transistor [package="TO92 [THT]"]
  R1 = Resistor [tolerance=±5% power=0.25W resistance=1000 package=THT]
  D1 = Rectifier Diode [part_number=1N4001 package="300 mil [THT]"]
  M1 = RioRand LM2596
  WATER_PUMP1 = water pump/motor
  Part2 = 16x8 LED Matrix Backpack [part_number=2038]
  Part3 = 16x8 LED Matrix Backpack [part_number=2038]
  M2 = RioRand LM2596
  Part4 = Adafruit STEMMA Soil Sensor - I2C Capacitive Moisture Sensor [part_number="Adafruit #4026"]
  Power_plug1 = Power plug

nets:
  N1: Part1.3.3V, M2.Pin_3
  N2: Part1.IO26, R1.Pin_0
  N3: Part1.IO14, IC1.IN_2
  N4: Part1.IO12, IC1.IN_1
  5V: Part1.5V, Part4.VIN
  GND: Part1.GND, IC1.GND, Q1.C, M2.Pin_4, Part4.GND
  N5: Part1.IO22, Part4.SDA
  N6: Part1.IO21, Part4.SCL
  N7: IC1.+_OUT_1, Part3.VDD
  N8: IC1.-_OUT_1, Part3.GND
  N9: IC1.+_OUT_2, Part2.VDD
  N10: IC1.-_OUT_2, Part2.GND
  N11: IC1.-_VIN, M1.Pin_2, M2.Pin_2, Power_plug1.GND
  N12: IC1.+_VIN, D1.cathode, M1.Pin_1, M2.Pin_1, Power_plug1.VCC
  N13: Q1.E, R1.Pin_1
  N14: Q1.B, D1.anode, WATER_PUMP1.pin_1
  N15: M1.Pin_3, WATER_PUMP1.pin_2

notes:
  Output set to 5V for submersible pump
  Output set to 3.3V to power the ESP32
  Modified part, taking place of grow light panels from amazon
  12V 5A wall plug

custom parts:
  Picobuck: The PicoBuck LED Driver is an economical and easy to use driver that will allow you to control and blend three different LEDs on three different channels. By default, each channel is driven at 330mA; that current can be reduced by either presenting an analog voltage or a PWM signal to the board. Version 12 of the board adds a solderable jumper that can be closed to increase the maximum current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
  water pump/motor: WATER PUMP BY ARDUBLOCKTR
  16x8 LED Matrix Backpack: This 16x8 monochrome LED matrix includes a driver chip for simple control via an I2C interface. The backpack features address-selection jumpers so you can connect up to eight matrices on a single I2C bus.
  Adafruit STEMMA Soil Sensor - I2C Capacitive Moisture Sensor: Most low cost soil sensors are resistive style, where there's two prongs and the sensor measures the conductivity between the two. These work OK at first, but eventually start to oxidize because of the exposed metal. Even if they're gold plated! The resistivity measurement goes up and up, so you constantly have to re-calibrate your code. Also, resistive measurements don't always work in loose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
